# Fritzing sketch blink (saved by Fritzing 0.9.2b)

parts:
  Part1 = Arduino Board Ethernet
  Part2 = Humidity Sensor - HIH-4030 Breakout
  LED1 = LED - 5mm [color="Red (633nm)" package="5 mm [THT]"]
  R1 = Resistor [tolerance=±5% resistance=220 package="0603 [SMD]"]

nets:
  N1: Part1.D13/SCK, R1.Pin_1
  GND: Part1.GND, Part2.GND, LED1.cathode
  N2: Part1.A0, Part2.OUT
  5V: Part1.5V, Part2.VCC
  N3: LED1.anode, R1.Pin_0

notes:
  LED is a water pump

// code stored in the sketch: blink.ino
// the setup function runs once when you press reset or power the board
void setup() {
  // initialize digital pin 13 as an output.
  pinMode(13, OUTPUT);
}

// the loop function runs over and over again forever
void loop() {
  digitalWrite(13, HIGH);   // turn the LED on (HIGH is the voltage level)
  delay(1000);              // wait for a second
  digitalWrite(13, LOW);    // turn the LED off by making the voltage LOW
  delay(1000);              // wait for a second
}
