# Fritzing sketch pump_when_needed_arduino (saved by Fritzing 0.9.2b)

parts:
  Part1 = Arduino Board Ethernet
  Part2 = Humidity Sensor - HIH-4030 Breakout
  LED1 = LED - 5mm [color="Red (633nm)" package="5 mm [THT]"]
  R1 = Resistor [tolerance=±5% resistance=220 package="0603 [SMD]"]

nets:
  N1: Part1.D13/SCK, R1.Pin_1
  GND: Part1.GND, Part2.GND, LED1.cathode
  N2: Part1.A0, Part2.OUT
  5V: Part1.5V, Part2.VCC
  N3: LED1.anode, R1.Pin_0

notes:
  LED is a water pump

// code stored in the sketch: blink.ino
// the setup function runs once when you press reset or power the board
int sensorPin = 14;  // A0
int humidity_value = 0;
int humidity_low = 70;   // max 710
int times_pumped = 0;

void setup() {
  pinMode(sensorPin, INPUT);
  // initialize digital pin 13 as an output.
  pinMode(13, OUTPUT);
  Serial.begin(9600);
}

// the loop function runs over and over again forever
void loop() {
  digitalWrite(13, LOW);    // turn the LED off by making the voltage LOW
  delay(2000);              // wait for a second
  humidity_value = analogRead(sensorPin);
  Serial.println(humidity_value);
  times_pumped = 0;
  while ((humidity_value <= humidity_low) && (times_pumped < 5)) {
    digitalWrite(13, HIGH);
    delay(1000);
    humidity_value = analogRead(sensorPin);
    times_pumped += 1;
    Serial.println(humidity_value);
  };
}

// code stored in the sketch: pump_when_needed_arduino.ino
// the setup function runs once when you press reset or power the board
int sensorPin = 14;  // A0
int humidity_value = 0;
int humidity_low = 70;   // max 710
int times_pumped = 0;

void setup() {
  pinMode(sensorPin, INPUT);
  // initialize digital pin 13 as an output.
  pinMode(13, OUTPUT);
  Serial.begin(9600);
}

// the loop function runs over and over again forever
void loop() {
  digitalWrite(13, LOW);    // turn the LED off by making the voltage LOW
  delay(2000);              // wait for a second
  humidity_value = analogRead(sensorPin);
  Serial.println(humidity_value);
  times_pumped = 0;
  while ((humidity_value <= humidity_low) && (times_pumped < 5)) {
    digitalWrite(13, HIGH);
    delay(1000);
    humidity_value = analogRead(sensorPin);
    times_pumped += 1;
    Serial.println(humidity_value);
  };
}
